# Fritzing sketch mpr121 (saved by Fritzing 0.9.3b)
breadboards: 1

parts:
  U1 = atmega328 [package=dip]
  C1 = Ceramic Capacitor [capacitance="100 nF" package="0805 [SMD, multilayer]"]
  LED1 = LED - 3mm [color="Yellow (595nm)" package="3 mm [THT]"]
  R1 = Resistor [tolerance=±5% resistance=220 package="1206 [SMD]"]
  IC1 = Voltage Regulator [package=to-220-alt]
  Part1 = MPR121 Breakout
  R2 = Resistor [tolerance=±5% resistance=4.7k package="1206 [SMD]"]
  R3 = Resistor [tolerance=±5% resistance=4.7k package="1206 [SMD]"]
  VCC1 = 4 x AAA Battery Mount
  USB1 = Wiring USB Adapter

nets:
  N1: U1.D0_(RX), USB1.RX, USB1.5V
  N2: U1.D1_(TX), USB1.TX
  N3: U1.D2, Part1.~IRQ
  N4: U1.VCC, C1.0, IC1.OUT, VCC1.+
  GND: U1.GND#7, C1.1, R1.Pin_1, IC1.GND, Part1.GND, VCC1.-, USB1.GND
  N5: U1.D8, LED1.anode
  N6: U1.A4, Part1.SDA, R2.Pin_1
  N7: U1.A5, Part1.SCL, R3.Pin_0
  N8: LED1.cathode, R1.Pin_0
  N9: IC1.IN, Part1.3.3V, R2.Pin_0, R3.Pin_1
